# Fritzing sketch BatteryHarness (saved by Fritzing 0.8.0b)
stripboards: 5

parts:
  U1 = Voltage Regulator - 5V [package="TO220 [THT]"]  # not connected
  U2 = Voltage Regulator - 5V [package="DPak [SMD]"]  # not connected
  J1 = female pin header, 3 pins [form="♀ (female)"]
  J2 = female pin header, 3 pins [form="♀ (female)"]
  J3 = female pin header, 3 pins [form="♀ (female)"]
  U3 = Voltage Regulator - 5V [package="DPak [SMD]"]  # not connected
  C2 = Ceramic Capacitor [capacitance=100nF package="100 mil [THT, multilayer]"]
  J5 = female pin header, 7 pins [form="♀ (female)"]
  J4 = female pin header, 7 pins [form="♀ (female)"]
  J6 = female pin header, 3 pins [form="♀ (female)"]
  J7 = female pin header, 3 pins [form="♀ (female)"]
  J8 = female pin header, 3 pins [form="♀ (female)"]
  J9 = female pin header, 3 pins [form="♀ (female)"]
  J11 = female pin header, 2 pins [form="♀ (female)"]
  J12 = female pin header, 5 pins [form="♀ (female)"]  # not connected
  J13 = female pin header, 5 pins [form="♀ (female)"]  # not connected
  J14 = female pin header, 7 pins [form="♀ (female)"]
  J15 = female pin header, 3 pins [form="♀ (female)"]
  J16 = female pin header, 3 pins [form="♀ (female)"]
  J17 = female pin header, 2 pins [form="♀ (female)"]
  J18 = female pin header, 2 pins [form="♀ (female)"]

nets:
  N1: J1.pin1, J5.pin7, J4.pin7, J14.pin7
  N2: J1.pin2, J2.pin2, J3.pin1, C2.0, J5.pin5, J4.pin5, J11.pin1, J14.pin5, J17.pin2, J18.pin1
  N3: J1.pin3, J5.pin6, J4.pin6, J14.pin6
  N4: J2.pin3, J17.pin1
  N5: J3.pin2, J11.pin2, J18.pin2
  N6: J3.pin3, C2.1
  N7: J5.pin1, J5.pin2, J5.pin3
  N8: J4.pin1, J4.pin2, J4.pin3
  N9: J6.pin1, J7.pin1
  N10: J6.pin2, J7.pin2
  N11: J6.pin3, J7.pin3
  N12: J8.pin1, J9.pin1
  N13: J8.pin2, J9.pin2
  N14: J8.pin3, J9.pin3
  N15: J14.pin1, J14.pin2, J14.pin3
  N16: J15.pin1, J16.pin1
  N17: J15.pin2, J16.pin2
  N18: J15.pin3, J16.pin3
