# Fritzing sketch IR detection circuit (saved by Fritzing 0.8.0b)
stripboards: 3

parts:
  Q1 = NPN-Transistor [package="TO92 [THT]"]
  C1 = Ceramic Capacitor [capacitance=470pF package="200 mil [THT, multilayer]"]
  IC3 = DIP - 8 pins [chip_label=TL082 package="DIP (Dual Inline) [THT]"]
  IC4 = DIP - 8 pins [chip_label=TL082 package="DIP (Dual Inline) [THT]"]
  R3 = Resistor [tolerance=±5% resistance=220 package=THT]
  R5 = Resistor [tolerance=±5% resistance=220 package=THT]
  C2 = Ceramic Capacitor [capacitance=100nF package="100 mil [THT, multilayer]"]
  R6 = Resistor [tolerance=±5% resistance=220 package=THT]
  C3 = Ceramic Capacitor [capacitance=100nF package="100 mil [THT, multilayer]"]
  R7 = Resistor [tolerance=±5% resistance=220 package=THT]
  IC6 = DIP - 8 pins [chip_label=TL082 package="DIP (Dual Inline) [THT]"]
  D1 = Zener Diode [part_number=1N4732A breakdown_voltage=3.6V package="300 mil [THT]"]
  D2 = Zener Diode [part_number=1N4732A breakdown_voltage=3.6V package="300 mil [THT]"]
  R2 = Resistor [tolerance=±5% resistance=47k package=THT]
  R1 = Resistor [tolerance=±5% resistance=500 package=THT]
  R10 = Rotary Potentiometer (Small)
  IC5 = DIP - 8 pins [chip_label=TL082 package="DIP (Dual Inline) [THT]"]
  C4 = Ceramic Capacitor [capacitance=100nF package="100 mil [THT, multilayer]"]
  C6 = Ceramic Capacitor [capacitance=100nF package="100 mil [THT, multilayer]"]
  R11 = Resistor [tolerance=±5% resistance=220 package=THT]
  R12 = Resistor [tolerance=±5% resistance=220 package=THT]
  C7 = Ceramic Capacitor [capacitance=100nF package="100 mil [THT, multilayer]"]

nets (from the schematic view):
  N1: Q1.E, IC3.1IN+, R1.Pin_0
  9V: Q1.C, IC3.VCC+, IC4.VCC+, IC6.VCC+, IC5.VCC+
  N2: C1.0, IC3.2IN+, R2.Pin_0
  N3: C1.1, IC3.1OUT, IC3.1IN-
  GND: IC3.VCC-, IC4.1IN+, IC4.VCC-, IC6.VCC-, D2.anode, R2.Pin_1, R1.Pin_1, IC5.1IN+, IC5.VCC-, IC5.2IN+
  N4: IC3.2IN-, IC3.2OUT, R3.Pin_0
  N5: IC4.1OUT, IC4.2IN+, R10.wiper
  N6: IC4.1IN-, R3.Pin_1, R10.leg1
  N7: IC4.2IN-, IC4.2OUT, R5.Pin_0
  N8: C2.0, IC5.1IN-
  N9: R6.Pin_0, C3.0
  N10: R6.Pin_1, C3.1, R7.Pin_1, IC5.1OUT
  N11: R7.Pin_0, C4.1
  N12: IC6.1OUT, D1.anode
  N13: IC6.1IN-, IC6.2IN+, D1.cathode, C6.1, R11.Pin_1
  N14: IC6.1IN+, R12.Pin_1, C7.1
  N15: IC6.2IN-, IC6.2OUT, D2.cathode
  N16: IC5.2OUT, C4.0, C7.0
  N17: C6.0, R11.Pin_0

custom parts:
  DIP - 8 pins: A DIP stand-in part for whatever IC you want. With 8 pins on a 300mil dual inline package (DIP) footprint.
