# Fritzing sketch IR sensor (saved by Fritzing 0.8.0b)
stripboards: 6

parts:
  Q1 = NPN-Transistor [package="TO92 [THT]"]
  IC1 = DIP - 8 pins [chip_label=TL082 package="DIP (Dual Inline) [THT]"]
  R1 = Resistor [tolerance=±5% resistance=500 package=THT]
  R2 = Resistor [tolerance=±5% resistance=500 package=THT]
  C2 = Ceramic Capacitor [capacitance=470pF package="100 mil [THT, multilayer]"]  # not connected
  C3 = Ceramic Capacitor [capacitance=0.47nF package="100 mil [THT, multilayer]"]
  R3 = Resistor [tolerance=±5% resistance=10k package=THT]
  IC2 = DIP - 8 pins [chip_label=TL082 package="DIP (Dual Inline) [THT]"]
  R4 = Resistor [tolerance=±5% resistance=220 package=THT]
  R5 = Resistor [tolerance=±5% resistance=220 package=THT]
  C4 = Ceramic Capacitor [capacitance=100nF package="100 mil [THT, multilayer]"]
  IC3 = DIP - 8 pins [chip_label=TL082 package="DIP (Dual Inline) [THT]"]  # not connected

nets:
  N1: Q1.E, IC1.2IN+, R1.Pin_1
  N2: Q1.C, IC1.VCC+, R1.Pin_0, IC2.VCC+
  N3: IC1.1OUT, IC1.1IN-, R3.Pin_1
  N4: IC1.1IN+, R2.Pin_1, C3.0
  N5: IC1.VCC-, IC2.1IN+, IC2.VCC-
  N6: IC1.2IN-, IC1.2OUT, C3.1
  N7: R3.Pin_0, IC2.1IN-, R4.Pin_1
  N8: IC2.1OUT, IC2.2IN+, R4.Pin_0
  N9: IC2.2IN-, IC2.2OUT, R5.Pin_1
  N10: R5.Pin_0, C4.1

custom parts:
  DIP - 8 pins: A DIP stand-in part for whatever IC you want. With 8 pins on a 300mil dual inline package (DIP) footprint.
