# Fritzing sketch Miniature H-bridge (saved by Fritzing 0.8.0b)
stripboards: 5

parts:
  IC1 = DIP - 8 pins [chip_label=LM311 package="DIP (Dual Inline) [THT]"]
  R1 = Resistor [tolerance=±5% resistance=33k package=THT]
  Q1 = NPN-Transistor [package="TO92 [THT]"]
  R2 = Resistor [tolerance=±5% resistance=10k package=THT]
  IC2 = DIP - 8 pins [chip_label=LM311 package="DIP (Dual Inline) [THT]"]
  Q3 = NPN-Transistor [package="TO92 [THT]"]
  R4 = Resistor [tolerance=±5% resistance=33k package=THT]
  R3 = Resistor [tolerance=±5% resistance=10k package=THT]
  Q4 = Basic FET P-Channel [package="TO220 [THT]"]
  Q5 = Basic FET P-Channel [package="TO220 [THT]"]

nets (from the schematic view):
  GND: IC1.GND, IC1.VEE, Q1.E, IC2.GND, IC2.VEE, Q3.E
  Signal 1: IC1.IN+
  5V: IC1.IN-, R1.Pin_1, IC2.IN-, R4.Pin_1
  N1: IC1.OUT, R1.Pin_0, Q1.B
  15V: IC1.VCC, R2.Pin_0, IC2.VCC, R3.Pin_0, Q4.source, Q5.source
  N2: Q1.C, R2.Pin_1, Q4.gate
  Signal 2: IC2.IN+
  N3: IC2.OUT, Q3.B, R4.Pin_0
  N4: Q3.C, R3.Pin_1, Q5.gate
  Output 1: Q4.drain
  Output 2: Q5.drain

custom parts:
  DIP - 8 pins: A DIP stand-in part for whatever IC you want. With 8 pins on a 300mil dual inline package (DIP) footprint.
